// Logisim project 7 segmentosvm.circ as structural Verilog
module _7segmentos (
  input  in_1,
  input  in_2,
  input  in_3,
  input  in_4
);

  wire or_1_out, or_2_out, or_3_out, or_4_out, or_5_out, or_6_p4, or_7_out, or_8_out, or_9_out;

  or or_1 (or_1_out, ~in_2, ~in_3);  // OR_Gate
  or or_2 (or_2_out, in_2, in_4);
  or or_3 (or_3_out, ~in_3, ~in_4);  // OR_Gate
  or or_4 (or_4_out, in_3, in_4);
  buf or_5 (or_5_out, ~in_1);  // OR_Gate OR_Gate
  // OR_Gate or_6: pin names not known; wires that end beside it: or_3_out, or_1_out, or_5_out, or_6_p4
  or or_7 (or_7_out, in_1, in_3, or_1_out, or_2_out);
  or or_8 (or_8_out, in_2, or_3_out, or_4_out);
  or or_9 (or_9_out, in_2, in_3, in_4);
  // OR_Gate or_10 has open pins: in0=in_1, in1=or_6_p4, out=open
  // AND_Gate and_1 is placed but not wired
  // AND_Gate and_2 is placed but not wired
  // AND_Gate and_3 is placed but not wired
  // AND_Gate and_4 is placed but not wired
  // AND_Gate and_5 is placed but not wired
  // AND_Gate and_6 is placed but not wired
  // NAND_Gate nand_1 is placed but not wired
  // AND_Gate and_7 is placed but not wired
endmodule
