// Logisim project Logisim Projetos Circuitos.circ as structural Verilog
module AD_1 (
  input  A,
  input  B,
  input  Vem_1,
  output S,
  output Vai_1
);

  wire and_1_out, and_2_out, or_1_out, xor_1_out;

  xor xor_1 (xor_1_out, A, B);
  or or_1 (or_1_out, B, Vem_1);
  xor xor_2 (S, xor_1_out, Vem_1);
  and and_1 (and_1_out, or_1_out, A);
  and and_2 (and_2_out, B, Vem_1);
  or or_2 (Vai_1, and_1_out, and_2_out);
endmodule

module ADD_2 (
  input  in_1,
  input  in_2,
  input  in_3
);

  main main_1 ();
  AD_1 ad_1_1 (.Vem_1(1'b0), .Vai_1(in_3));  // open: A, B, S
endmodule
