// Logisim project MEMORIAROM2.circ as structural Verilog
module _7segmentos (
  input  in_1,
  input  in_2,
  input  in_3,
  input  in_4
);

  wire or_1_out, or_2_out, or_3_out, or_4_out, or_5_out, or_6_out, or_7_out, or_8_out, or_9_out, or_10_out;

  or or_1 (or_1_out, ~in_2, ~in_3);  // OR_Gate
  or or_2 (or_2_out, in_2, in_4);
  or or_3 (or_3_out, ~in_3, ~in_4);  // OR_Gate
  or or_4 (or_4_out, in_3, in_4);
  buf or_5 (or_5_out, ~in_1);  // OR_Gate OR_Gate
  or or_6 (or_6_out, or_5_out, or_1_out, or_3_out);
  or or_7 (or_7_out, in_1, in_3, or_1_out, or_2_out);
  or or_8 (or_8_out, in_2, or_3_out, or_4_out);
  or or_9 (or_9_out, in_2, in_3, in_4);
  or or_10 (or_10_out, in_1, or_6_out);
  // AND_Gate and_1 is placed but not wired
  // AND_Gate and_2: pin names not known; wires that end beside it: or_7_out, or_8_out
  // AND_Gate and_3 is placed but not wired
  // AND_Gate and_4 is placed but not wired
  // AND_Gate and_5 is placed but not wired
  // AND_Gate and_6 is placed but not wired
  // NAND_Gate nand_1 is placed but not wired
  // AND_Gate and_7 is placed but not wired
endmodule

module MEMORIAROM (
);

  wire clock_1_out;
  wire [3:0] counter_1_q;
  wire [4:0] rom_1_data, shift_register_1_out, shift_register_1_q0, shift_register_1_q1, shift_register_1_q2,
       shift_register_1_q3, shift_register_1_q4, shift_register_2_out, shift_register_2_q0,
       shift_register_2_q1, shift_register_2_q2, shift_register_2_q3, shift_register_2_q4,
       shift_register_2_q5, shift_register_2_q6, shift_register_2_q7, shift_register_3_q0,
       shift_register_3_q4, shift_register_3_q5, shift_register_3_q6, shift_register_3_q7;

  Counter #(.width(4), .max('hf)) counter_1 (.Q(counter_1_q), .clr(clock_1_out));  // open: load, D, count, carry, clk
  ROM #(.addrWidth(4), .dataWidth(5)) rom_1 (.addr(counter_1_q), .data(rom_1_data));  // open: sel
  Clock #(.highDuration(5), .lowDuration(5)) clock_1 (.out(clock_1_out));
  Shift_Register #(.width(5)) shift_register_1 (
    .in(rom_1_data), .clk(clock_1_out), .out(shift_register_1_out), .q0(shift_register_1_q0),
    .q1(shift_register_1_q1), .q2(shift_register_1_q2), .q3(shift_register_1_q3), .q4(shift_register_1_q4),
    .q5(shift_register_1_q0), .q6(shift_register_1_q0), .q7(shift_register_1_q0));  // open: shift, load, clr, d0, d1, d2, d3, d4, d5, d6, d7
  DotMatrix #(.matrixcols(8), .matrixrows(5)) dotmatrix_1 (
    .col0(shift_register_1_q0), .col1(shift_register_1_q1), .col2(shift_register_1_q2),
    .col3(shift_register_1_q3), .col4(shift_register_1_q4), .col5(shift_register_1_q0),
    .col6(shift_register_1_q0), .col7(shift_register_1_q0));
  Shift_Register #(.width(5)) shift_register_2 (
    .in(shift_register_1_out), .clk(clock_1_out), .out(shift_register_2_out), .q0(shift_register_2_q0),
    .q1(shift_register_2_q1), .q2(shift_register_2_q2), .q3(shift_register_2_q3), .q4(shift_register_2_q4),
    .q5(shift_register_2_q5), .q6(shift_register_2_q6), .q7(shift_register_2_q7));  // open: shift, load, clr, d0, d1, d2, d3, d4, d5, d6, d7
  DotMatrix #(.matrixcols(8), .matrixrows(5)) dotmatrix_2 (
    .col0(shift_register_3_q4), .col1(shift_register_3_q4), .col2(shift_register_3_q4),
    .col3(shift_register_3_q4), .col4(shift_register_3_q4), .col5(shift_register_3_q4),
    .col6(shift_register_3_q4), .col7(shift_register_3_q4));
  Shift_Register #(.width(5)) shift_register_3 (
    .in(shift_register_2_out), .clk(clock_1_out), .q0(shift_register_3_q0), .q1(shift_register_3_q0),
    .q2(shift_register_3_q0), .q3(shift_register_3_q0), .q4(shift_register_3_q4), .q5(shift_register_3_q5),
    .q6(shift_register_3_q6), .q7(shift_register_3_q7));  // open: shift, out, load, clr, d0, d1, d2, d3, d4, d5, d6, d7
  DotMatrix #(.matrixcols(8), .matrixrows(5)) dotmatrix_3 (
    .col0(shift_register_3_q4), .col1(shift_register_3_q4), .col2(shift_register_3_q4),
    .col3(shift_register_3_q4), .col4(shift_register_3_q4), .col5(shift_register_3_q5),
    .col6(shift_register_3_q6), .col7(shift_register_3_q7));

  // Notes on the sheet:
  //   contents of rom_1 (hex, n*v repeats v):
  //   1f 14 1f 0 1f 15 1f 0 11 11 1f 0 1f 11 1f
endmodule

module LOAD (
);

  wire j_k_ff_1_qn, j_k_ff_3_qn;
  wire [2:0] j_k_ff_3_q;

  J_K_Flip_Flop j_k_ff_1 (
    .J(j_k_ff_3_qn), .K(j_k_ff_3_qn), .Q(j_k_ff_3_q[2]), .Qn(j_k_ff_1_qn));  // open: clk, preset, en, reset
  J_K_Flip_Flop j_k_ff_2 (
    .J(j_k_ff_3_q[2]), .clk(j_k_ff_3_qn), .K(1'b1), .Q(j_k_ff_3_q[1]));  // open: Qn, preset, en, reset
  J_K_Flip_Flop j_k_ff_3 (
    .J(j_k_ff_1_qn), .clk(j_k_ff_3_qn), .K(j_k_ff_3_q[1]), .Q(j_k_ff_3_q[0]), .Qn(j_k_ff_3_qn));  // open: preset, en, reset
endmodule
