// Logisim project MION.circ as structural Verilog
module S (
  input  [3:0] in_1,
  output out_2
);

  wire and_1_out, and_2_out, and_3_out, and_4_out;

  and and_1 (and_1_out, in_1[3], in_1[2], in_1[0]);
  and and_2 (and_2_out, in_1[3], in_1[0], in_1[3]);
  and and_3 (and_3_out, in_1[3], in_1[2], in_1[3]);
  and and_4 (and_4_out, in_1[3], in_1[0], in_1[2]);
  or or_1 (out_2, and_1_out, and_2_out, and_3_out, and_4_out);

  assign in_1[1] = in_1[3];
endmodule
